// Logisim project 1221026_1220423_1220060 (2).circ as structural Verilog: 4 circuits, main circuit ALU
module ALU (
  input  [31:0] input_2,
  input  [31:0] input_1,
  input  [3:0] ALU_OP,
  output [31:0] ALU_Result
);

  wire comparator_1_eq, comparator_2_lt;
  wire [31:0] adder_1_out, AND_out, bit_extender_1_out, bit_extender_2_out, CAND_out, not_1_out, OR_out,
       shifter_1_out, shifter_2_out, shifter_3_out, shifter_4_out, subtractor_1_out, XOR_out;

  assign not_1_out = ~input_1;  // NOT_Gate not_1, 32 bits wide
  assign XOR_out = input_1 ^ input_2;  // XOR_Gate XOR, 32 bits wide
  assign AND_out = input_1 & input_2;  // AND_Gate AND, 32 bits wide
  assign OR_out = input_1 | input_2;  // OR_Gate OR, 32 bits wide
  assign CAND_out = not_1_out & input_2;  // AND_Gate CAND, 32 bits wide
  Adder #(.width(32)) adder_1 (.a(input_1), .b(input_2), .out(adder_1_out));  // open: cin, cout
  Comparator #(.width(32)) comparator_1 (.a(input_1), .b(input_2), .eq(comparator_1_eq));  // open: gt, lt
  Subtractor #(.width(32)) subtractor_1 (.a(input_2), .b(input_1), .out(subtractor_1_out));  // open: bin, bout
  Comparator #(.width(32)) comparator_2 (.a(input_1), .b(input_2), .lt(comparator_2_lt));  // open: gt, eq
  Shifter #(.width(32), .shift("ar")) shifter_1 (.in(input_1), .\dist (input_2[4:0]), .out(shifter_1_out));
  Shifter #(.width(32), .shift("lr")) shifter_2 (.in(input_1), .\dist (input_2[4:0]), .out(shifter_2_out));
  Shifter #(.width(32)) shifter_3 (.in(input_1), .\dist (input_2[4:0]), .out(shifter_3_out));
  Shifter #(.width(32), .shift("rr")) shifter_4 (.in(input_1), .\dist (input_2[4:0]), .out(shifter_4_out));
  assign bit_extender_1_out = {{31{comparator_1_eq}}, comparator_1_eq};  // Bit_Extender bit_extender_1
  assign bit_extender_2_out = {{31{comparator_2_lt}}, comparator_2_lt};  // Bit_Extender bit_extender_2
  Multiplexer #(.select(4), .width(32), .enable("false")) multiplexer_1 (
    .in0(XOR_out), .in1(AND_out), .in2(OR_out), .in3(CAND_out), .in4(adder_1_out), .in5(bit_extender_1_out),
    .in6(subtractor_1_out), .in7(bit_extender_2_out), .in8(shifter_1_out), .in9(shifter_2_out),
    .in10(shifter_3_out), .in11(shifter_4_out), .out(ALU_Result), .sel(ALU_OP));  // open: in12, in13, in14, in15
endmodule

module RFile (
  input  [2:0] Ry,
  input  [2:0] Rz,
  input  [31:0] bus_x,
  input  [2:0] Rx,
  input  RegWrite,
  input  in_6,
  output [31:0] bus_y,
  output [31:0] bus_z
);

  wire and_1_out, and_2_out, and_3_out, and_4_out, and_5_out, and_6_out, and_7_out, decoder_1_out0,
       decoder_2_out0, decoder_2_out1, decoder_2_out2, decoder_2_out3, decoder_2_out4, decoder_2_out5,
       decoder_2_out6, decoder_2_out7, decoder_3_out0, decoder_3_out1, decoder_3_out2, decoder_3_out3,
       decoder_3_out4, decoder_3_out5, decoder_3_out6, decoder_3_out7, R1, R2, R3, R4, R5, R6, R7;
  wire [31:0] Reg1_q, Reg2_q, Reg3_q, Reg4_q, Reg5_q, Reg6_q, Reg7_q;

  Decoder #(.select(3), .enable("false")) decoder_1 (
    .out0(decoder_1_out0), .out1(R1), .out2(R2), .out3(R3), .out4(R4), .out5(R5), .out6(R6), .out7(R7),
    .sel(Rx));
  Register #(.width(32)) Reg1 (.D(bus_x), .en(and_1_out), .Q(Reg1_q), .clk(in_6));  // open: clr
  and and_1 (and_1_out, R1, RegWrite);
  Register #(.width(32)) Reg2 (.D(bus_x), .en(and_2_out), .Q(Reg2_q), .clk(in_6));  // open: clr
  and and_2 (and_2_out, R2, RegWrite);
  Register #(.width(32)) Reg3 (.D(bus_x), .en(and_3_out), .Q(Reg3_q), .clk(in_6));  // open: clr
  and and_3 (and_3_out, R3, RegWrite);
  Register #(.width(32)) Reg4 (.D(bus_x), .en(and_4_out), .Q(Reg4_q), .clk(in_6));  // open: clr
  and and_4 (and_4_out, R4, RegWrite);
  Register #(.width(32)) Reg5 (.D(bus_x), .en(and_5_out), .Q(Reg5_q), .clk(in_6));  // open: clr
  and and_5 (and_5_out, R5, RegWrite);
  Register #(.width(32)) Reg6 (.D(bus_x), .en(and_6_out), .Q(Reg6_q), .clk(in_6));  // open: clr
  and and_6 (and_6_out, R6, RegWrite);
  Register #(.width(32)) Reg7 (.D(bus_x), .en(and_7_out), .Q(Reg7_q), .clk(in_6));  // open: clr
  and and_7 (and_7_out, R7, RegWrite);
  assign bus_y = decoder_2_out0 ? {32{1'b0}} : 32'bz;  // Controlled_Buffer controlled_buffer_1
  assign bus_y = decoder_2_out1 ? Reg1_q : 32'bz;  // Controlled_Buffer controlled_buffer_2
  assign bus_y = decoder_2_out2 ? Reg2_q : 32'bz;  // Controlled_Buffer controlled_buffer_3
  assign bus_y = decoder_2_out3 ? Reg3_q : 32'bz;  // Controlled_Buffer controlled_buffer_4
  assign bus_y = decoder_2_out4 ? Reg4_q : 32'bz;  // Controlled_Buffer controlled_buffer_5
  assign bus_y = decoder_2_out5 ? Reg5_q : 32'bz;  // Controlled_Buffer controlled_buffer_6
  assign bus_y = decoder_2_out6 ? Reg6_q : 32'bz;  // Controlled_Buffer controlled_buffer_7
  assign bus_y = decoder_2_out7 ? Reg7_q : 32'bz;  // Controlled_Buffer controlled_buffer_8
  Decoder #(.select(3), .enable("false")) decoder_2 (
    .out0(decoder_2_out0), .out1(decoder_2_out1), .out2(decoder_2_out2), .out3(decoder_2_out3),
    .out4(decoder_2_out4), .out5(decoder_2_out5), .out6(decoder_2_out6), .out7(decoder_2_out7), .sel(Ry));
  assign bus_z = decoder_3_out0 ? {32{1'b0}} : 32'bz;  // Controlled_Buffer controlled_buffer_9
  assign bus_z = decoder_3_out1 ? Reg1_q : 32'bz;  // Controlled_Buffer controlled_buffer_10
  assign bus_z = decoder_3_out2 ? Reg2_q : 32'bz;  // Controlled_Buffer controlled_buffer_11
  assign bus_z = decoder_3_out3 ? Reg3_q : 32'bz;  // Controlled_Buffer controlled_buffer_12
  assign bus_z = decoder_3_out4 ? Reg4_q : 32'bz;  // Controlled_Buffer controlled_buffer_13
  assign bus_z = decoder_3_out5 ? Reg5_q : 32'bz;  // Controlled_Buffer controlled_buffer_14
  assign bus_z = decoder_3_out6 ? Reg6_q : 32'bz;  // Controlled_Buffer controlled_buffer_15
  assign bus_z = decoder_3_out7 ? Reg7_q : 32'bz;  // Controlled_Buffer controlled_buffer_16
  Decoder #(.select(3), .enable("false")) decoder_3 (
    .out0(decoder_3_out0), .out1(decoder_3_out1), .out2(decoder_3_out2), .out3(decoder_3_out3),
    .out4(decoder_3_out4), .out5(decoder_3_out5), .out6(decoder_3_out6), .out7(decoder_3_out7), .sel(Rz));
endmodule

module SOP (
);

  wire clock_1_out, ExtOP, memRead, memWrite, opcode, RegDst, RegWrite;
  wire [1:0] B_Selction, f, pcOpcode, WriteBack__a_data;
  wire [2:0] imm3, multiplexer_2_out;
  wire [3:0] alu_op;
  wire [4:0] bit_extender_1_out, bit_extender_2_out, imm3imm2, Imm5, op, shift_Imm5, shifter_1_out;
  wire [4:2] imm5_t;
  wire [7:5] imm11_t;
  wire [10:0] Imm11, shift_Imm11;
  wire [19:0] ex_Imm5, ex_Imm11, multiplexer_1_out, PC, PC_2, pc_2_t, PC_ex_Imm5, PC_ex_Imm11;
  wire [31:0] _0Extend_Imm5, alu_1_alu_result, bit_extender_6_out, bit_extender_9_out, bit_extender_10_out,
       ex_Imm11ALU, multiplexer_3_out, multiplexer_4_out, multiplexer_5_out, multiplexer_6_out, ram_1_data,
       rfile_1_bus_y, rfile_1_bus_z, RY_Imm2_Imm3, SExtend_Imm5;

  Adder #(.width(20)) adder_1 (.a(PC), .b(ex_Imm5), .out(PC_ex_Imm5));  // open: cin, cout
  Adder #(.width(20)) adder_2 (.a(PC), .b(ex_Imm11), .out(PC_ex_Imm11));  // open: cin, cout
  Adder #(.width(20)) adder_3 (.a(PC), .b(20'h2), .out(PC_2));  // open: cin, cout
  Multiplexer #(.select(2), .width(20), .enable("false")) multiplexer_1 (
    .in0(PC_2), .in1(PC_ex_Imm5), .in2(PC_ex_Imm11), .out(multiplexer_1_out), .sel(pcOpcode));  // open: in3
  Register #(.width(20)) u_PC (.D(multiplexer_1_out), .en(1'b1), .Q(PC), .clk(clock_1_out));  // open: clr
  Clock clock_1 (.out(clock_1_out));
  assign bit_extender_1_out = {{2{1'b0}}, imm3};  // Bit_Extender bit_extender_1
  Shifter #(.width(5)) shifter_1 (.in(bit_extender_1_out), .\dist (3'b010), .out(shifter_1_out));
  assign bit_extender_2_out = {{3{1'b0}}, f};  // Bit_Extender bit_extender_2
  ROM #(.addrWidth(20), .dataWidth(16)) rom_1 (.addr(PC), .data({op, imm3, imm11_t, imm5_t, f}));  // open: sel
  Adder #(.width(5)) adder_4 (.a(shifter_1_out), .b(bit_extender_2_out), .out(imm3imm2));  // open: cin, cout
  assign _0Extend_Imm5 = {{27{1'b0}}, Imm5};  // Bit_Extender bit_extender_3
  assign SExtend_Imm5 = {{27{Imm5[4]}}, Imm5};  // Bit_Extender bit_extender_4
  Shifter #(.width(5)) shifter_2 (.in(Imm5), .\dist (3'b001), .out(shift_Imm5));
  assign ex_Imm5 = {{15{shift_Imm5[4]}}, shift_Imm5};  // Bit_Extender bit_extender_5
  Multiplexer #(.width(3), .enable("false")) multiplexer_2 (
    .in0(imm3), .in1(3'b111), .out(multiplexer_2_out), .sel(RegDst));
  RFile rfile_1 (
    .Ry(imm11_t), .Rz(imm5_t), .bus_x(multiplexer_6_out), .RegWrite(RegWrite), .bus_y(rfile_1_bus_y),
    .in_6(clock_1_out), .bus_z(rfile_1_bus_z), .Rx(multiplexer_2_out));
  assign bit_extender_6_out = {{27{imm3imm2[4]}}, imm3imm2};  // Bit_Extender bit_extender_6
  Shifter #(.width(11)) shifter_3 (.in(Imm11), .\dist (4'b0001), .out(shift_Imm11));
  assign ex_Imm11 = {{9{shift_Imm11[10]}}, shift_Imm11};  // Bit_Extender bit_extender_7
  assign ex_Imm11ALU = {{21{shift_Imm11[10]}}, shift_Imm11};  // Bit_Extender bit_extender_8
  Adder #(.width(32)) adder_5 (.a(bit_extender_6_out), .b(rfile_1_bus_y), .out(RY_Imm2_Imm3));  // open: cin, cout
  assign bit_extender_9_out = {{27{imm3imm2[4]}}, imm3imm2};  // Bit_Extender bit_extender_9
  Multiplexer #(.width(32), .enable("false")) multiplexer_3 (
    .in0(_0Extend_Imm5), .in1(SExtend_Imm5), .out(multiplexer_3_out), .sel(ExtOP));
  Multiplexer #(.select(2), .width(32), .enable("false")) multiplexer_4 (
    .in0(rfile_1_bus_z), .in1(bit_extender_9_out), .in2(ex_Imm11ALU), .in3(multiplexer_3_out),
    .out(multiplexer_4_out), .sel(B_Selction));
  ALU alu_1 (.ALU_Result(alu_1_alu_result), .input_1(multiplexer_4_out), .input_2(rfile_1_bus_y), .ALU_OP(alu_op));
  Multiplexer #(.width(32), .enable("false")) multiplexer_5 (
    .in0(alu_1_alu_result), .in1(RY_Imm2_Imm3), .out(multiplexer_5_out), .sel(opcode));
  RAM #(.addrWidth(20), .dataWidth(32), .bus("separate")) ram_1 (
    .addr(multiplexer_5_out[19:0]), .din(rfile_1_bus_z), .data(ram_1_data), .str(memRead), .clk(clock_1_out),
    .ld(memWrite));  // open: sel, clr
  assign bit_extender_10_out = {{12{pc_2_t[19]}}, pc_2_t};  // Bit_Extender bit_extender_10
  Multiplexer #(.select(2), .width(32), .enable("false")) multiplexer_6 (
    .in0(alu_1_alu_result), .in1(ram_1_data), .in2(bit_extender_10_out), .in3(RY_Imm2_Imm3),
    .out(multiplexer_6_out), .sel(WriteBack__a_data));

  // Other names for the same wires on the sheet: imm2[1:0] = f; imm5_t[1:0] = f;
  //   imm11_t (some bits) = {imm3, imm5_t, f}; z[2:0] = imm5_t; y[2:0] = imm11_t; x[2:0] = imm3
endmodule

module CountrolUnit (
  input  [4:0] OPcode
);

  wire [11:0] rom_1_data;

  ROM #(.addrWidth(5), .dataWidth(12)) rom_1 (.addr(OPcode), .data(rom_1_data));  // open: sel
endmodule
